# Fritzing sketch diagram (saved by Fritzing 1.0.6)
# 18650 Li-ion Battery: CC-BY Dr Kristofer Chan, King's College London/Remote-research.org
circuit board: 8.46667cm x 5.64444cm

parts:
  OLED_I2C1 = OLED 128x64 I2C Monochrome Display
  J1 = Piezo Speaker
  TP1 = TP4056 [chip_label=TP4056 package="DIP (Dual Inline) [THT]"]
  L1 = Solenoid
  U1 = ESP32 Dev_Kit [part_number=ESP32S-HiLetgo]
  BAT1 = 18650 Li-ion Battery [package=battery-18650]
  Q1 = MOSFET-NCHANNEL [package=to220v]
  ZS-042_RTC1 = ZS-042 RTC Module
  RE1 = KY-040 Rotary encoder [package="Breakout board"]

nets:
  N1: OLED_I2C1.SDA, U1.GPIO21, ZS-042_RTC1.SDA
  N2: OLED_I2C1.SCK, U1.GPIO22, ZS-042_RTC1.SCL
  VCC: OLED_I2C1.VDD, L1.pin2, U1.3.3, ZS-042_RTC1.VCC, RE1.Vcc
  GND: OLED_I2C1.GND, TP1.pin6, U1.GND, Q1.S, ZS-042_RTC1.GND, RE1.GND
  N3: J1.pin1, L1.pin1, Q1.D
  N4: J1.pin2, TP1.pin3, U1.VIN
  N5: TP1.pin4, BAT1.-
  N6: TP1.pin5, BAT1.+
  N7: U1.GPIO14, RE1.SW
  N8: U1.GPIO12, Q1.G
  N9: U1.GPIO18, RE1.CLK
  N10: U1.GPIO19, RE1.DT

custom parts:
  TP4056: A DIP stand-in part for whatever IC you want. With 6 pins on a 300mil dual inline package (DIP) footprint.
  18650 Li-ion Battery: 18650 li-ion Battery Standard 18650 battery with interactive connectors Creative Common Attribution 4.0 International (CC-BY 4.0) license. Any use of this part requires attribution of Dr Kristofer Chan, Department of Geography, King's College London. Contact kristofer.chan [at] kcl.ac.uk OR kris [at] remote-research.org for further information.
  KY-040 Rotary encoder: KY-040 Rotary Encoder with switch on breakout borad from AZ Delivery
